# Fritzing sketch MEx-Raspi-Connector (saved by Fritzing 0.9.3b)
circuit board: 3.78896cm x 5.47664cm
breadboards: 1

parts:
  Raspberry_Pi_3 = Raspberry Pi 3 [part_number=RPI-3-V1.2]
  MG996 = Basic Servo
  90GL = Basic Servo
  90GU = Basic Servo
  L9110s = L9110 H-bridge module [part_number="L9110 H-bridge"]
  M1 = DC Motor
  M2 = DC Motor
  INDICATOR = RGB LED (com. cathode, rbg) [package="5 mm [THT]"]
  EXPW = Battery block 12V

nets:
  GND: Raspberry_Pi_3.GND, MG996.gnd, 90GL.gnd, 90GU.gnd, L9110s.GND, INDICATOR.common_cathode, EXPW.-
  N1: Raspberry_Pi_3.GIPO5, INDICATOR.green_anode
  N2: Raspberry_Pi_3.GIPO6, INDICATOR.blue_anode
  N3: Raspberry_Pi_3.GIPO13, INDICATOR.red_anode
  N4: Raspberry_Pi_3.GIPO21, L9110s.A-IA
  N5: Raspberry_Pi_3.GIPO20, L9110s.A-IB
  N6: Raspberry_Pi_3.GIPO16, L9110s.B-IA
  N7: Raspberry_Pi_3.GIPO12, L9110s.B-IB
  N8: Raspberry_Pi_3.GIPO18, 90GU.pulse
  N9: Raspberry_Pi_3.GIPO15, 90GL.pulse
  N10: Raspberry_Pi_3.GIPO14, MG996.pulse
  VCC: Raspberry_Pi_3.5V, MG996.vcc, 90GL.vcc, 90GU.vcc
  N11: L9110s.VCC, EXPW.+
  N12: L9110s.MOTOR_A-A, M1.pin_2
  N13: L9110s.MOTOR_A-B, M1.pin_1
  N14: L9110s.MOTOR_B-A, M2.pin_2
  N15: L9110s.MOTOR_B-B, M2.pin_1

notes:
  Todo:
  Indicator.B = 5
  Indicator.G = 6

custom parts:
  Battery block 12V: Your standard 12 Volts battery block
