# Fritzing sketch RemoteControllerRouting (saved by Fritzing 0.9.3b)
stripboards: 2

parts:
  WeMos_D1 = WeMos D1 Mini
  Part1 = Arduino Uno (Rev3)
  BUZZER = Piezo Speaker
  LEFT_BTN = Pushbutton [package="[THT]"]
  R1 = Resistor [tolerance=±5% resistance=1k package=THT]
  BUZZ_BTN = Pushbutton [package="[THT]"]
  R2 = Resistor [tolerance=±5% resistance=1k package=THT]
  PARK_BTN = Pushbutton [package="[THT]"]
  R3 = Resistor [tolerance=±5% resistance=1k package=THT]
  RIGH_BTN = Pushbutton [package="[THT]"]
  R4 = Resistor [tolerance=±5% resistance=1k package=THT]
  LEFT = smd LED [color="Blue (430nm)" package="1206 [SMD]"]
  BUZZ = smd LED [color="Blue (430nm)" package="1206 [SMD]"]
  PARK = smd LED [color="Blue (430nm)" package="1206 [SMD]"]
  RIGH = smd LED [color="Blue (430nm)" package="1206 [SMD]"]
  SPEED = Trimmer Potentiometer [maximum_resistance=10kΩ package=THT]
  WHEEL = Trimmer Potentiometer [maximum_resistance=10kΩ package=THT]
  GL3 = Trimmer Potentiometer [maximum_resistance=10kΩ package=THT]
  GR3 = Trimmer Potentiometer [maximum_resistance=10kΩ package=THT]
  BRAKE = Trimmer Potentiometer [maximum_resistance=10kΩ package=THT]
  HANDBRAKE = Trimmer Potentiometer [maximum_resistance=10kΩ package=THT]

nets:
  5V: WeMos_D1.5V, Part1.VIN
  N1: WeMos_D1.D4, Part1.D3_PWM
  N2: WeMos_D1.D5, Part1.D2
  N3: WeMos_D1.G, Part1.GND, BUZZER.pin1, R1.Pin_1, R2.Pin_1, R3.Pin_1, R4.Pin_1, LEFT.cathode, BUZZ.cathode, PARK.cathode, RIGH.cathode, SPEED.leg1, WHEEL.leg1, GL3.leg1, GR3.leg1, BRAKE.leg1, HANDBRAKE.leg1
  N4: Part1.A0, SPEED.wiper
  N5: Part1.A1, BRAKE.wiper
  N6: Part1.A2, GR3.wiper
  N7: Part1.A3, HANDBRAKE.wiper
  N8: Part1.A4/SDA, GL3.wiper
  N9: Part1.A5/SCL, WHEEL.wiper
  N10: Part1.D9_PWM, BUZZER.pin2
  N11: Part1.D10_PWM/SS, RIGH.anode
  N12: Part1.D11_PWM/MOSI, PARK.anode
  N13: Part1.D12/MISO, BUZZ.anode
  N14: Part1.D13/SCK, LEFT.anode
  N15: Part1.D4, RIGH_BTN.Pin_1, RIGH_BTN.Pin_2, R4.Pin_0
  N16: Part1.D5_PWM, PARK_BTN.Pin_1, PARK_BTN.Pin_2, R3.Pin_0
  N17: Part1.D6_PWM, BUZZ_BTN.Pin_1, BUZZ_BTN.Pin_2, R2.Pin_0
  N18: Part1.D7, LEFT_BTN.Pin_1, LEFT_BTN.Pin_2, R1.Pin_0
  N19: Part1.5V, LEFT_BTN.Pin_3, LEFT_BTN.Pin_4, BUZZ_BTN.Pin_3, BUZZ_BTN.Pin_4, PARK_BTN.Pin_3, PARK_BTN.Pin_4, RIGH_BTN.Pin_3, RIGH_BTN.Pin_4, SPEED.leg2, WHEEL.leg2, GL3.leg2, GR3.leg2, BRAKE.leg2, HANDBRAKE.leg2
