# Fritzing sketch arduino&wemos (saved by Fritzing 0.9.3b)
stripboards: 2

parts:
  Part1 = Arduino Uno (Rev3) - ICSP
  WeMos_D1_Mini1 = WeMos D1 Mini
  LED1 = LED - 5mm [color="Red (633nm)" package="5 mm [THT]"]
  LED2 = LED - 5mm [color="Red (633nm)" package="5 mm [THT]"]
  LED3 = LED - 5mm [color="Red (633nm)" package="5 mm [THT]"]
  LED4 = LED - 5mm [color="Red (633nm)" package="5 mm [THT]"]
  S8 = Pushbutton [package="[THT]"]
  S9 = Pushbutton [package="[THT]"]
  S10 = Pushbutton [package="[THT]"]
  S11 = Pushbutton [package="[THT]"]
  R1 = Resistor [tolerance=±5% resistance=220 package=THT]
  R2 = Resistor [tolerance=±5% resistance=220 package=THT]
  R3 = Resistor [tolerance=±5% resistance=220 package=THT]
  R4 = Resistor [tolerance=±5% resistance=220 package=THT]
  J1 = Piezo Speaker
  RE1 = Rotary Encoder [package=THT]
  RE2 = Rotary Encoder [package=THT]
  RE3 = Rotary Encoder [package=THT]
  RE4 = Rotary Encoder [package=THT]
  RE5 = Rotary Encoder [package=THT]
  RE6 = Rotary Encoder [package=THT]

nets:
  N1: Part1.A0, RE1.EncoderPinC
  N2: Part1.A1, RE2.EncoderPinC
  N3: Part1.A2, RE3.EncoderPinC
  N4: Part1.A3, RE4.EncoderPinC
  N5: Part1.A4/SDA, RE5.EncoderPinC
  N6: Part1.A5/SCL, RE6.EncoderPinC
  N7: Part1.5V, LED1.cathode, LED2.cathode, LED3.cathode, LED4.cathode, R1.Pin_1, R2.Pin_1, R3.Pin_1, R4.Pin_1, RE1.EncoderPinB, RE2.EncoderPinB, RE3.EncoderPinB, RE4.EncoderPinB, RE5.EncoderPinB, RE6.EncoderPinB
  N8: Part1.D9_PWM, J1.pin2
  N9: Part1.D10_PWM/SS, LED4.anode
  N10: Part1.D11_PWM/MOSI, LED3.anode
  N11: Part1.D12/MISO, LED2.anode
  N12: Part1.D13/SCK, LED1.anode
  N13: Part1.GND, WeMos_D1_Mini1.G, S8.Pin_1, S8.Pin_2, S9.Pin_1, S9.Pin_2, S10.Pin_1, S10.Pin_2, S11.Pin_1, S11.Pin_2, J1.pin1, RE1.EncoderPinA, RE2.EncoderPinA, RE3.EncoderPinA, RE4.EncoderPinA, RE5.EncoderPinA, RE6.EncoderPinA
  N14: Part1.D2, WeMos_D1_Mini1.D5
  N15: Part1.D3_PWM, WeMos_D1_Mini1.D4
  N16: Part1.D4, S8.Pin_3, S8.Pin_4, R4.Pin_0
  N17: Part1.D5_PWM, S9.Pin_3, S9.Pin_4, R3.Pin_0
  N18: Part1.D6_PWM, S10.Pin_3, S10.Pin_4, R2.Pin_0
  N19: Part1.D7, S11.Pin_3, S11.Pin_4, R1.Pin_0
  VIN: Part1.VIN, WeMos_D1_Mini1.5V

// code stored in the sketch: Untitled.ino

