# Fritzing sketch demo controller (saved by Fritzing 0.9.3b)
breadboards: 1

parts:
  LED1 = LED - 5mm [color="Red (633nm)" package="5 mm [THT]"]
  LED2 = LED - 5mm [color="Red (633nm)" package="5 mm [THT]"]
  S1 = Pushbutton [package="[THT]"]
  S2 = Pushbutton [package="[THT]"]
  Part1 = Arduino Uno (Rev3) - ICSP
  WeMos_D1_Mini1 = WeMos D1 Mini
  R3 = Resistor [tolerance=±5% resistance=220 package=THT]
  R4 = Resistor [tolerance=±5% resistance=220 package=THT]
  R5 = Resistor [tolerance=±5% resistance=220 package=THT]
  R6 = Resistor [tolerance=±5% resistance=220 package=THT]

nets:
  N1: LED1.cathode, Part1.D13/SCK
  N2: LED1.anode, R5.Pin_0
  N3: LED2.cathode, S1.Pin_1, S1.Pin_2, S2.Pin_1, S2.Pin_2, Part1.GND, R3.Pin_0, R4.Pin_0, R5.Pin_1, R6.Pin_1
  N4: LED2.anode, R6.Pin_0
  N5: S1.Pin_3, S1.Pin_4, S2.Pin_3, S2.Pin_4, Part1.5V
  N6: Part1.D2, WeMos_D1_Mini1.D5
  N7: Part1.D3_PWM, WeMos_D1_Mini1.D4
  N8: Part1.D4, R4.Pin_1
  N9: Part1.D5_PWM, R3.Pin_1
